# Fritzing sketch Deska (saved by Fritzing 0.8.7b)
circuit board: 14.0553cm x 8.53016cm
perfboards: 3

parts:
  7_Segment2 = 7 Segment Display
  7_Segment3 = 7 Segment Display
  7_Segment4 = 7 Segment Display
  Q1 = pnp-Powertransistor [package="TO220 [THT]"]
  Q2 = pnp-Powertransistor [package="TO220 [THT]"]
  Q3 = pnp-Powertransistor [package="TO220 [THT]"]
  Q4 = pnp-Powertransistor [package="TO220 [THT]"]
  R1 = Resistor [tolerance=±5% resistance=220 package=THT]
  R2 = Resistor [tolerance=±5% resistance=220 package=THT]
  R3 = Resistor [tolerance=±5% resistance=220 package=THT]
  R4 = Resistor [tolerance=±5% resistance=220 package=THT]
  R5 = Resistor [tolerance=±5% resistance=220 package=THT]
  R6 = Resistor [tolerance=±5% resistance=220 package=THT]
  R7 = Resistor [tolerance=±5% resistance=220 package=THT]
  R8 = Resistor [tolerance=±5% resistance=220 package=THT]
  R9 = Resistor [tolerance=±5% resistance=220 package=THT]
  R10 = Resistor [tolerance=±5% resistance=220 package=THT]
  R11 = Resistor [tolerance=±5% resistance=220 package=THT]
  R12 = Resistor [tolerance=±5% resistance=220 package=THT]
  S1 = SWITCH-MOMENTARY-2 [package=tactile_switch_smd-2]
  S2 = SWITCH-MOMENTARY-2 [package=tactile_switch_smd-2]
  S3 = SWITCH-MOMENTARY-2 [package=tactile_switch_smd-2]
  S4 = SWITCH-MOMENTARY-2 [package=tactile_switch_smd-2]
  S5 = SWITCH-MOMENTARY-2 [package=tactile_switch_smd-2]
  S6 = SWITCH-MOMENTARY-2 [package=tactile_switch_smd-2]
  S7 = SWITCH-MOMENTARY-2 [package=tactile_switch_smd-2]
  S8 = SWITCH-MOMENTARY-2 [package=tactile_switch_smd-2]
  S9 = SWITCH-MOMENTARY-2 [package=tactile_switch_smd-2]
  S10 = SWITCH-MOMENTARY-2 [package=tactile_switch_smd-2]
  S11 = SWITCH-MOMENTARY-2 [package=tactile_switch_smd-2]
  S12 = SWITCH-MOMENTARY-2 [package=tactile_switch_smd-2]
  U1 = RELAY [package=relay-jzc]
  7_Segment1 = 7 Segment Display
  JP6 = Header 12 [package=1x12_machine-pin-header_lock.004]
  JP7 = Header 12 [package=1x12_machine-pin-header_lock.004]
  JP8 = Header 12 [package=1x12_machine-pin-header_lock.004]
  JP9 = Header 12 [package=1x12_machine-pin-header_lock.004]

nets:
  N1: 7_Segment2.Segment_G, 7_Segment3.Segment_G, 7_Segment4.Segment_G, R7.Pin_1, 7_Segment1.Segment_G
  N2: 7_Segment2.Segment_F, 7_Segment3.Segment_F, 7_Segment4.Segment_F, R6.Pin_1, 7_Segment1.Segment_F
  N3: 7_Segment2.common_anode, Q2.collector
  N4: 7_Segment2.Segment_E, 7_Segment3.Segment_E, 7_Segment4.Segment_E, R5.Pin_1, 7_Segment1.Segment_E
  N5: 7_Segment2.Segment_D, 7_Segment3.Segment_D, 7_Segment4.Segment_D, R4.Pin_1, 7_Segment1.Segment_D
  N6: 7_Segment2.Segment_DP, 7_Segment3.Segment_DP, 7_Segment4.Segment_DP, R8.Pin_1, 7_Segment1.Segment_DP
  N7: 7_Segment2.Segment_C, 7_Segment3.Segment_C, 7_Segment4.Segment_C, R3.Pin_1, 7_Segment1.Segment_C
  N8: 7_Segment2.Segment_B, 7_Segment3.Segment_B, 7_Segment4.Segment_B, R2.Pin_1, 7_Segment1.Segment_B
  N9: 7_Segment2.Segment_A, 7_Segment3.Segment_A, 7_Segment4.Segment_A, R1.Pin_1, 7_Segment1.Segment_A
  N10: 7_Segment3.common_anode, Q3.collector
  N11: 7_Segment4.common_anode, Q4.collector
  N12: Q1.base, R12.Pin_1
  N13: Q1.collector, 7_Segment1.common_anode
  N14: Q1.emitter, Q2.emitter, Q3.emitter, Q4.emitter, JP7.12
  N15: Q2.base, R11.Pin_1
  N16: Q3.base, R10.Pin_1
  N17: Q4.base, R9.Pin_1
  N18: R1.Pin_0, JP8.8
  N19: R2.Pin_0, JP8.7
  N20: R3.Pin_0, JP8.6
  N21: R4.Pin_0, JP8.5
  N22: R5.Pin_0, JP8.4
  N23: R6.Pin_0, JP8.3
  N24: R7.Pin_0, JP8.2
  N25: R8.Pin_0, JP8.1
  N26: R9.Pin_0, JP7.1
  N27: R10.Pin_0, JP7.2
  N28: R11.Pin_0, JP7.3
  N29: R12.Pin_0, JP7.4
  N30: S1.2, S2.2, S3.2, S4.2, S5.2, S6.2, S7.2, S8.2, S9.2, S10.2, S11.2, S12.2, JP6.12
  N31: S1.1, JP6.8
  N32: S2.1, JP6.7
  N33: S3.1, JP6.6
  N34: S4.1, JP6.5
  N35: S5.1, JP6.4
  N36: S6.1, JP6.3
  N37: S7.1, JP6.2
  N38: S8.1, JP6.1
  N39: S9.1, JP7.8
  N40: S10.1, JP7.7
  N41: S11.1, JP7.6
  N42: S12.1, JP7.5
  N43: U1.COIL2, U1.NC, JP9.1
  N44: U1.NO, U1.COIL1, JP9.9
